# Fritzing sketch electrical_connections (saved by Fritzing 0.9.3b)
circuit board: 8.46667cm x 5.64444cm
breadboards: 1

parts:
  S2 = Pushbutton [package="[THT]"]
  S3 = Pushbutton [package="[THT]"]
  Arduino = Arduino Uno (Rev3)
  R6 = Resistor [tolerance=±5% resistance=10k package=THT]
  R7 = Resistor [tolerance=±5% resistance=15k package=THT]
  Raspberry_Pi_1 = Raspberry Pi 3 [part_number=RPI-3-V1.2]
  J1 = Basic Servo
  J2 = Basic Servo
  J3 = Basic Servo
  J4 = Basic Servo
  J5 = Basic Servo
  J6 = Basic Servo
  S1 = Pushbutton [package="[THT]"]
  J8 = female pin header, 4 pins [form="♀ (female)"]
  R1 = Resistor [tolerance=±5% resistance=10k package=THT]
  R2 = Resistor [tolerance=±5% resistance=10k package=THT]
  R3 = Resistor [tolerance=±5% resistance=10k package=THT]
  R4 = Resistor [tolerance=±5% resistance=10k package=THT]
  J10 = female pin header, 6 pins [form="♀ (female)"]
  S1_2 = male pin header, 3 pins [form="♂ (male)"]
  S2_2 = male pin header, 3 pins [form="♂ (male)"]
  S3_2 = male pin header, 3 pins [form="♂ (male)"]
  S6 = male pin header, 3 pins [form="♂ (male)"]
  S5 = male pin header, 3 pins [form="♂ (male)"]
  S4 = male pin header, 3 pins [form="♂ (male)"]
  S4_2 = Pushbutton [package="[THT]"]
  VCC1 = Battery
  J11 = Screw terminal - 2 pins [package=THT]
  J7 = female pin header, 2 pins [form="♀ (female)"]
  J12 = female pin header, 5 pins [form="♀ (female)"]

nets:
  N1: S2.Pin_1, S2.Pin_2, Arduino.D4, J8.pin2, R2.Pin_0
  N2: S2.Pin_3, S2.Pin_4, S3.Pin_3, S3.Pin_4, Arduino.5V, S1.Pin_3, S1.Pin_4, S4_2.Pin_3, S4_2.Pin_4, J7.pin1
  N3: S3.Pin_1, S3.Pin_2, Arduino.D7, J8.pin3, R3.Pin_0
  N4: Arduino.D8, J8.pin4, R4.Pin_0, S4_2.Pin_1, S4_2.Pin_2
  N5: Arduino.D9_PWM, J4.pulse, J10.pin4, S4.pin3
  N6: Arduino.D10_PWM/SS, J5.pulse, J10.pin5, S5.pin3
  N7: Arduino.D11_PWM/MOSI, J6.pulse, J10.pin6, S6.pin3
  GND: Arduino.GND, R7.Pin_1, Raspberry_Pi_1.GND, J1.gnd, J2.gnd, J3.gnd, J4.gnd, J5.gnd, J6.gnd, R1.Pin_1, R2.Pin_1, R3.Pin_1, R4.Pin_1, S1_2.pin1, S2_2.pin1, S3_2.pin1, S6.pin1, S5.pin1, S4.pin1, VCC1.-, J11.pin1, J7.pin2, J12.pin5
  N8: Arduino.D0/RX, Raspberry_Pi_1.GPIO14, J12.pin1, J12.pin4
  N9: Arduino.D1/TX, R6.Pin_0, J12.pin2
  N10: Arduino.D2, S1.Pin_1, S1.Pin_2, J8.pin1, R1.Pin_0
  N11: Arduino.D3_PWM, J1.pulse, J10.pin1, S1_2.pin3
  N12: Arduino.D5_PWM, J2.pulse, J10.pin2, S2_2.pin3
  N13: Arduino.D6_PWM, J3.pulse, J10.pin3, S3_2.pin3
  N14: R6.Pin_1, R7.Pin_0, Raspberry_Pi_1.GPIO15, J12.pin3
  VCC: J1.vcc, J2.vcc, J3.vcc, J4.vcc, J5.vcc, J6.vcc, S1_2.pin2, S2_2.pin2, S3_2.pin2, S6.pin2, S5.pin2, S4.pin2, VCC1.+, J11.pin2

notes:
  Robotic Manipulator with Computer Vision
  Willian Beraldi Esperandio - 2019
  A-GND
  A-Vcc
  Power Plug
  Servos
  - Angle
  + Angle
  + Joint
  - Joint
  output
  Arduno
  Vcc
  GND
  PTX
  PRX
  ARX
  ATX
  Serial
  Communication
